# Fritzing sketch Sketch Fritzing (saved by Fritzing 0.9.3b)
breadboards: 3

parts:
  Part2 = Arduino Mega ADK (Rev3)
  hc-sr1 = hc-sr04
  U1 = SBX DSUN [package=THT]
  Part3 = KY-033 Tracing Black White Line Hunting Sensor Module For Arduino
  Pololu_A2 = DRV 8825 Stepper Motor Carrier, High Current [part_number="DRV 8825"]
  S1 = Round Pushbutton
  S2 = Round Pushbutton
  S3 = Taiway 100-SP-X-T1 SPDT Miniature Toggle Switch [part_number=100-SP-X-T1-0-0-B1-M1 package=THT]
  J1 = Basic Servo
  M1 = Stepper Motor - Bipolar
  C1 = Capacitor Polarized [package=cpol-radial-100uf-25v]
  M2 = Stepper Motor - Bipolar
  IR1 = TSOP312.., 314.. [package=THT]
  IR2 = TSOP312.., 314.. [package=THT]
  hc-sr2 = hc-sr04
  hc-sr3 = hc-sr04
  hc-sr4 = hc-sr04
  R1 = Resistor [tolerance=±5% resistance=220 package="2010 [SMD]"]
  LED2 = LEDs [package=led10mm]
  Pololu_A1 = DRV 8825 Stepper Motor Carrier, High Current [part_number="DRV 8825"]
  VCC1 = Battery block 9V

nets (from the breadboard view):
  N1: Part2.A8, Part3.S
  N2: Part2.D18/TX1, S2.leg1
  N3: Part2.GND, R1.Pin_0
  N4: Part2.D12_PWM, Pololu_A1.STEP
  N5: Part2.D11_PWM, Pololu_A1.DIRECTION
  N6: Part2.D10_PWM, Pololu_A2.STEP
  N7: Part2.D9_PWM, Pololu_A2.DIRECTION
  N8: Part2.D8_PWM, Pololu_A2.ENABLE, Pololu_A1.ENABLE
  N9: Part2.D2_PWM, IR1.Data
  N10: Part2.D3_PWM, IR2.Data
  N11: Part2.D4_PWM, IR1.Vs, IR2.Vs
  N12: Part2.D5_PWM, S1.leg1
  N13: Part2.D6_PWM, LED2.A
  N14: Part2.D7_PWM, J1.pulse
  N15: Part2.D44, hc-sr1.Echo
  N16: Part2.D45, hc-sr1.Trig
  N17: Part2.D46, hc-sr4.Echo
  N18: Part2.D47, hc-sr4.Trig
  N19: Part2.D48, hc-sr3.Echo
  N20: Part2.D49, hc-sr3.Trig
  N21: Part2.D50/MISO, hc-sr2.Echo
  N22: Part2.D51/MOSI, hc-sr2.Trig
  VCC: hc-sr1.VCC, U1.+VOUT, Part3.V+, Pololu_A2.MS1, Pololu_A2.MS2, J1.vcc, hc-sr2.VCC, hc-sr3.VCC, hc-sr4.VCC, Pololu_A1.MS1, Pololu_A1.MS2
  GND: hc-sr1.GND, U1.GND, Part3.GND, Pololu_A2.MS3, Pololu_A2.GROUND_ST/_MT, Pololu_A2.GROUND_LOG, S1.leg0, S2.leg0, S3.L2, J1.gnd, C1.+, C1.-, IR1.GND, IR2.GND, hc-sr2.GND, hc-sr3.GND, hc-sr4.GND, Pololu_A1.MS3, Pololu_A1.GROUND_ST/_MT, Pololu_A1.GROUND_LOG
  N23: U1.+VIN, Pololu_A2.VOLTAGE_ST/_MT, Pololu_A1.VOLTAGE_ST/_MT, VCC1.+
  N24: Pololu_A2.OUT_2B, M1.A
  N25: Pololu_A2.OUT_2A, M1.C
  N26: Pololu_A2.OUT_1A, M1.B
  N27: Pololu_A2.OUT_1B, M1.D
  N28: S3.COM, VCC1.-
  N29: M2.A, Pololu_A1.OUT_2B
  N30: M2.C, Pololu_A1.OUT_2A
  N31: M2.B, Pololu_A1.OUT_1A
  N32: M2.D, Pololu_A1.OUT_1B
  N33: R1.Pin_1, LED2.C

notes:
  Foi usado o modulo TCRT5000 em vez do KY033.
  11.1v
  5.0v
  STOP
  START

custom parts:
  SBX DSUN: SBX DSUN input voltage 4.5 - 28V DC output voltage .8v to 20VDC (step down converter) Output current 3A max
  KY-033 Tracing Black White Line Hunting Sensor Module For Arduino: Tracing Black White Line Hunting Sensor Module For Arduino Description: This is KY-033 tracking sensor. The KY-033 measures the intensity of infrared radiation and delivers it as an analog output voltage. Features: Operating voltage: 2.5 - 12V(cannot over12V) working current: 18mA-20mA at 5V Enhanced accuracy Documents: http://www.vishay.com/docs/83760/tcrt5000.pdf
