# Fritzing sketch Fritzing - Microrato (saved by Fritzing 0.9.3b)
breadboards: 1

parts:
  Part1 = Arduino Due (Rev2b)
  DRV_1 = DRV 8825 Stepper Motor Carrier, High Current [part_number="DRV 8825"]  # not connected
  M1 = Stepper Motor - Bipolar  # not connected
  J1 = Basic Servo
  S1 = Taiway 100-SP-X-T1 SPDT Miniature Toggle Switch [part_number=100-SP-X-T1-0-0-B1-M2 package=THT]
  S2 = Round Pushbutton
  LED1 = LED - 3mm [color="Red (633nm)" package="3 mm [THT]"]  # not connected
  LED2 = LEDs [package=led10mm]  # not connected
  U1 = LIPO-2000mAh [package=lipo-2000]
  C1 = Electrolytic Capacitor [capacitance=1µF package="100 mil [THT, electrolytic]"]
  S3 = Round Pushbutton
  DRV_2 = DRV 8825 Stepper Motor Carrier, High Current [part_number="DRV 8825"]  # not connected

nets:
  N1: Part1.D3_PWM, S2.leg0
  N2: Part1.D4_PWM/SS1, S3.leg0
  N3: Part1.D5_PWM, J1.pulse
  N4: J1.gnd, S1.L1, S2.leg1, C1.-, S3.leg1
  N5: J1.vcc, U1.+, C1.+
  N6: S1.L2, U1.-
