# Fritzing sketch Sketch Fritzing_recovered (saved by Fritzing 0.9.3b)
breadboards: 3

parts:
  hc-sr1 = hc-sr04
  U1 = SBX DSUN [package=THT]
  Part3 = KY-033 Tracing Black White Line Hunting Sensor Module For Arduino
  Pololu_A2 = DRV 8825 Stepper Motor Carrier, High Current [part_number="DRV 8825"]
  S1 = Round Pushbutton
  S2 = Round Pushbutton
  S3 = Taiway 100-SP-X-T1 SPDT Miniature Toggle Switch [part_number=100-SP-X-T1-0-0-B1-M1 package=THT]
  J1 = Basic Servo
  M1 = Stepper Motor - Bipolar
  C1 = Capacitor Polarized [package=cpol-radial-100uf-25v]
  M2 = Stepper Motor - Bipolar
  IR1 = TSOP312.., 314.. [package=THT]
  IR2 = TSOP312.., 314.. [package=THT]
  hc-sr2 = hc-sr04
  hc-sr3 = hc-sr04
  hc-sr4 = hc-sr04
  R1 = Resistor [tolerance=±5% resistance=220 package="2010 [SMD]"]
  LED2 = LEDs [package=led10mm]
  Pololu_A1 = DRV 8825 Stepper Motor Carrier, High Current [part_number="DRV 8825"]
  VCC1 = Battery block 9V
  WeMos_D1_Mini1 = WeMos D1 Mini
  Part2 = Arduino Mega ADK (Rev3)

nets:
  VCC: hc-sr1.VCC, U1.+VOUT, Part3.V+, Pololu_A2.MS1, Pololu_A2.MS2, J1.vcc, hc-sr2.VCC, hc-sr3.VCC, hc-sr4.VCC, Pololu_A1.MS1, Pololu_A1.MS2
  N1: hc-sr1.Trig, Part2.D45
  N2: hc-sr1.Echo, Part2.D44
  GND: hc-sr1.GND, U1.GND, Part3.GND, Pololu_A2.MS3, Pololu_A2.GROUND_ST/_MT, Pololu_A2.GROUND_LOG, S1.leg0, S2.leg0, S3.L2, J1.gnd, C1.+, C1.-, IR1.GND, IR2.GND, hc-sr2.GND, hc-sr3.GND, hc-sr4.GND, Pololu_A1.MS3, Pololu_A1.GROUND_ST/_MT, Pololu_A1.GROUND_LOG
  N3: U1.+VIN, Pololu_A2.VOLTAGE_ST/_MT, Pololu_A1.VOLTAGE_ST/_MT, VCC1.+
  N4: Part3.S, Part2.A8
  N5: Pololu_A2.ENABLE, Pololu_A1.ENABLE, Part2.D8_PWM
  N6: Pololu_A2.STEP, Part2.D10_PWM
  N7: Pololu_A2.DIRECTION, Part2.D9_PWM
  N8: Pololu_A2.OUT_2B, M1.A
  N9: Pololu_A2.OUT_2A, M1.C
  N10: Pololu_A2.OUT_1A, M1.B
  N11: Pololu_A2.OUT_1B, M1.D
  N12: S1.leg1, Part2.D5_PWM
  N13: S2.leg1, Part2.D18/TX1
  N14: S3.COM, VCC1.-
  N15: J1.pulse, Part2.D7_PWM
  N16: M2.A, Pololu_A1.OUT_2B
  N17: M2.C, Pololu_A1.OUT_2A
  N18: M2.B, Pololu_A1.OUT_1A
  N19: M2.D, Pololu_A1.OUT_1B
  N20: IR1.Vs, IR2.Vs, Part2.D4_PWM
  N21: IR1.Data, Part2.D2_PWM
  N22: IR2.Data, Part2.D3_PWM
  N23: hc-sr2.Trig, Part2.D51/MOSI
  N24: hc-sr2.Echo, Part2.D50/MISO
  N25: hc-sr3.Trig, Part2.D49
  N26: hc-sr3.Echo, Part2.D48
  N27: hc-sr4.Trig, Part2.D47
  N28: hc-sr4.Echo, Part2.D46
  N29: R1.Pin_0, Part2.GND#283, Part2.GND#308
  N30: R1.Pin_1, LED2.C
  N31: LED2.A, Part2.D6_PWM
  N32: Pololu_A1.STEP, Part2.D12_PWM
  N33: Pololu_A1.DIRECTION, Part2.D11_PWM
  5V: WeMos_D1_Mini1.5V, Part2.5V
  N34: WeMos_D1_Mini1.D1, Part2.RESET3
  N35: WeMos_D1_Mini1.G, Part2.GND#505
  N36: WeMos_D1_Mini1.RX, Part2.D1/TX0
  N37: WeMos_D1_Mini1.TX, Part2.D0/RX0

notes:
  Foi usado o modulo TCRT5000 em vez do KY033.
  11.1v
  5.0v
  STOP
  START
  LEFT
  RIGHT
  FRONT
  BACK
  FRONT LEFT
  FRONT RIGHT

custom parts:
  SBX DSUN: SBX DSUN input voltage 4.5 - 28V DC output voltage .8v to 20VDC (step down converter) Output current 3A max
  KY-033 Tracing Black White Line Hunting Sensor Module For Arduino: Tracing Black White Line Hunting Sensor Module For Arduino Description: This is KY-033 tracking sensor. The KY-033 measures the intensity of infrared radiation and delivers it as an analog output voltage. Features: Operating voltage: 2.5 - 12V(cannot over12V) working current: 18mA-20mA at 5V Enhanced accuracy Documents: http://www.vishay.com/docs/83760/tcrt5000.pdf
